# Fritzing sketch antenna (saved by Fritzing 0.9.2b)
circuit board: 20.5881cm x 23.2128cm
breadboards: 1

parts:
  Part1 = Arduino Nano (Rev3.0)
  U1 = Packages: [package=dil28-3]
  U2 = Packages: [package=dil28-3]
  LED8 = RGB LED (com. cathode, rgb) [package="5 mm [THT]"]
  LED9 = RGB LED (com. cathode, rgb) [package="5 mm [THT]"]
  LED10 = RGB LED (com. cathode, rgb) [package="5 mm [THT]"]
  LED11 = RGB LED (com. cathode, rgb) [package="5 mm [THT]"]
  LED12 = RGB LED (com. cathode, rgb) [package="5 mm [THT]"]
  LED13 = RGB LED (com. cathode, rgb) [package="5 mm [THT]"]
  R1 = Resistor [tolerance=±0.25% resistance=10k package=THT]
  R2 = Resistor [tolerance=±5% resistance=2.2k package=THT]
  R3 = Resistor [tolerance=±5% resistance=2.2k package=THT]
  R4 = Resistor [tolerance=±5% resistance=470 package=THT]
  R5 = Resistor [tolerance=±5% resistance=470 package=THT]
  R6 = Resistor [tolerance=±5% resistance=470 package=THT]
  R7 = Resistor [tolerance=±5% resistance=470 package=THT]
  R8 = Resistor [tolerance=±5% resistance=470 package=THT]
  R9 = Resistor [tolerance=±5% resistance=470 package=THT]
  R10 = Resistor [tolerance=±5% resistance=470 package=THT]
  R11 = Resistor [tolerance=±5% resistance=470 package=THT]
  R12 = Resistor [tolerance=±5% resistance=470 package=THT]
  R13 = Resistor [tolerance=±5% resistance=470 package=THT]
  R14 = Resistor [tolerance=±5% resistance=470 package=THT]
  R15 = Resistor [tolerance=±5% resistance=470 package=THT]
  R16 = Resistor [tolerance=±5% resistance=470 package=THT]
  R17 = Resistor [tolerance=±5% resistance=470 package=THT]
  R18 = Resistor [tolerance=±5% resistance=470 package=THT]
  R19 = Resistor [tolerance=±5% resistance=470 package=THT]
  R20 = Resistor [tolerance=±5% resistance=470 package=THT]
  R21 = Resistor [tolerance=±5% resistance=470 package=THT]
  V1 = DC Power [voltage=12V]
  Q1 = Basic FET P-Channel [package="TO220 [THT]"]
  Q2 = Basic FET P-Channel [package="TO220 [THT]"]
  Q3 = Basic FET P-Channel [package="TO220 [THT]"]
  Q4 = Basic FET P-Channel [package="TO220 [THT]"]
  Q5 = Basic FET P-Channel [package="TO220 [THT]"]
  Q6 = Basic FET P-Channel [package="TO220 [THT]"]
  Q7 = Basic FET P-Channel [package="TO220 [THT]"]
  Q8 = Basic FET P-Channel [package="TO220 [THT]"]
  Q9 = Basic FET P-Channel [package="TO220 [THT]"]
  Q10 = Basic FET P-Channel [package="TO220 [THT]"]
  Q11 = Basic FET P-Channel [package="TO220 [THT]"]
  Q12 = Basic FET P-Channel [package="TO220 [THT]"]
  Q13 = Basic FET P-Channel [package="TO220 [THT]"]
  Q14 = Basic FET P-Channel [package="TO220 [THT]"]
  Q15 = Basic FET P-Channel [package="TO220 [THT]"]
  Q16 = Basic FET P-Channel [package="TO220 [THT]"]
  Q17 = Basic FET P-Channel [package="TO220 [THT]"]
  Q18 = Basic FET P-Channel [package="TO220 [THT]"]

nets:
  GND: Part1.GND, U1.GND, U1.VPRG, U2.GND, U2.VPRG, R2.Pin_1, R3.Pin_1
  N1: Part1.D3, U1.GSCLK, U2.GSCLK
  N2: Part1.D9, U1.XLAT, U2.XLAT
  N3: Part1.D10, U1.BLANK, U2.BLANK, R1.Pin_0
  N4: Part1.D11/MOSI, U1.SIN
  VCC: Part1.5V, U1.DCPRG, U1.VCC, U2.DCPRG, U2.VCC, R1.Pin_1
  N5: Part1.D13/SCK, U1.SCLK, U2.SCLK
  N6: U1.OUT1, R6.Pin_0, Q3.gate
  N7: U1.OUT2, R5.Pin_0, Q2.gate
  N8: U1.OUT3, R7.Pin_0, Q5.gate
  N9: U1.OUT4, R9.Pin_0, Q6.gate
  N10: U1.OUT5, R8.Pin_0, Q4.gate
  N11: U1.OUT6, R10.Pin_0, Q8.gate
  N12: U1.OUT7, R12.Pin_0, Q7.gate
  N13: U1.OUT8, R11.Pin_0, Q9.gate
  N14: U1.OUT9, R13.Pin_0, Q10.gate
  N15: U1.OUT10, R15.Pin_0, Q11.gate
  N16: U1.OUT11, R14.Pin_0, Q12.gate
  N17: U1.OUT12, R16.Pin_0, Q13.gate
  N18: U1.OUT13, R18.Pin_0, Q15.gate
  N19: U1.OUT14, R17.Pin_0, Q14.gate
  N20: U1.OUT15, R19.Pin_0, Q17.gate
  N21: U1.SOUT, U2.SIN
  N22: U1.IREF, R2.Pin_0
  N23: U1.OUT0, R4.Pin_0, Q1.gate
  N24: U2.OUT1, R20.Pin_0, Q16.gate
  N25: U2.IREF, R3.Pin_0
  N26: U2.OUT0, R21.Pin_0, Q18.gate
  N27: LED8.red_anode, Q1.drain
  N28: LED8.common_cathode, LED9.common_cathode, LED10.common_cathode, LED11.common_cathode, LED12.common_cathode, LED13.common_cathode, R4.Pin_1, R5.Pin_1, R6.Pin_1, R7.Pin_1, R8.Pin_1, R9.Pin_1, R10.Pin_1, R11.Pin_1, R12.Pin_1, R13.Pin_1, R14.Pin_1, R15.Pin_1, R16.Pin_1, R17.Pin_1, R18.Pin_1, R19.Pin_1, R20.Pin_1, R21.Pin_1, V1.V+
  N29: LED8.green_anode, Q3.drain
  N30: LED8.blue_anode, Q2.drain
  N31: LED9.red_anode, Q5.drain
  N32: LED9.green_anode, Q6.drain
  N33: LED9.blue_anode, Q4.drain
  N34: LED10.red_anode, Q8.drain
  N35: LED10.green_anode, Q7.drain
  N36: LED10.blue_anode, Q9.drain
  N37: LED11.red_anode, Q10.drain
  N38: LED11.green_anode, Q11.drain
  N39: LED11.blue_anode, Q12.drain
  N40: LED12.red_anode, Q13.drain
  N41: LED12.green_anode, Q15.drain
  N42: LED12.blue_anode, Q14.drain
  N43: LED13.red_anode, Q17.drain
  N44: LED13.green_anode, Q18.drain
  N45: LED13.blue_anode, Q16.drain
  GND_2: V1.V-, Q1.source, Q2.source, Q3.source, Q4.source, Q5.source, Q6.source, Q7.source, Q8.source, Q9.source, Q10.source, Q11.source, Q12.source, Q13.source, Q14.source, Q15.source, Q16.source, Q17.source, Q18.source
